// Logisim project adapters.circ as structural Verilog
module dec_to_7seg (
  input  _0,
  input  _1,
  input  _2,
  input  _3,
  input  _4,
  input  _5,
  input  _6,
  input  _7,
  input  _8,
  input  _9,
  output right_bot,
  output bot,
  output left_bot,
  output mid,
  output left_top,
  output top,
  output right_top
);

  Transistor #(.\type ("n")) transistor_1 (.in(_0), .out(right_bot), .gate(_0));
  Transistor #(.\type ("n")) transistor_2 (.in(right_bot), .out(bot), .gate(_0));
  Transistor #(.\type ("n")) transistor_3 (.in(top), .out(left_top), .gate(_5));
  Transistor #(.\type ("n")) transistor_4 (.in(_5), .out(top), .gate(_5));
  Transistor #(.\type ("n")) transistor_5 (.in(bot), .out(left_bot), .gate(_0));
  Transistor #(.\type ("n")) transistor_6 (.in(left_bot), .out(left_top), .gate(_0));
  Transistor #(.\type ("n")) transistor_7 (.in(mid), .out(bot), .gate(_5));
  Transistor #(.\type ("n")) transistor_8 (.in(left_top), .out(mid), .gate(_5));
  Transistor #(.\type ("n")) transistor_9 (.in(left_top), .out(top), .gate(_0));
  Transistor #(.\type ("n")) transistor_10 (.in(top), .out(right_top), .gate(_0));
  Transistor #(.\type ("n")) transistor_11 (.in(bot), .out(right_bot), .gate(_5));
  Transistor #(.\type ("n")) transistor_12 (.in(_6), .out(left_top), .gate(_6));
  Transistor #(.\type ("n")) transistor_13 (.in(_1), .out(right_bot), .gate(_1));
  Transistor #(.\type ("n")) transistor_14 (.in(right_bot), .out(right_top), .gate(_1));
  Transistor #(.\type ("n")) transistor_15 (.in(mid), .out(left_bot), .gate(_6));
  Transistor #(.\type ("n")) transistor_16 (.in(left_top), .out(mid), .gate(_6));
  Transistor #(.\type ("n")) transistor_17 (.in(_2), .out(bot), .gate(_2));
  Transistor #(.\type ("n")) transistor_18 (.in(bot), .out(left_bot), .gate(_2));
  Transistor #(.\type ("n")) transistor_19 (.in(left_bot), .out(bot), .gate(_6));
  Transistor #(.\type ("n")) transistor_20 (.in(bot), .out(right_bot), .gate(_6));
  Transistor #(.\type ("n")) transistor_21 (.in(mid), .out(top), .gate(_2));
  Transistor #(.\type ("n")) transistor_22 (.in(left_bot), .out(mid), .gate(_2));
  Transistor #(.\type ("n")) transistor_23 (.in(_7), .out(right_top), .gate(_7));
  Transistor #(.\type ("n")) transistor_24 (.in(right_top), .out(top), .gate(_7));
  Transistor #(.\type ("n")) transistor_25 (.in(top), .out(right_top), .gate(_2));
  Transistor #(.\type ("n")) transistor_26 (.in(_3), .out(right_bot), .gate(_3));
  Transistor #(.\type ("n")) transistor_27 (.in(top), .out(right_bot), .gate(_7));
  Transistor #(.\type ("n")) transistor_28 (.in(bot), .out(mid), .gate(_3));
  Transistor #(.\type ("n")) transistor_29 (.in(right_bot), .out(bot), .gate(_3));
  Transistor #(.\type ("n")) transistor_30 (.in(_8), .out(right_top), .gate(_8));
  Transistor #(.\type ("n")) transistor_31 (.in(right_top), .out(top), .gate(_8));
  Transistor #(.\type ("n")) transistor_32 (.in(top), .out(right_top), .gate(_3));
  Transistor #(.\type ("n")) transistor_33 (.in(mid), .out(top), .gate(_3));
  Transistor #(.\type ("n")) transistor_34 (.in(top), .out(left_top), .gate(_8));
  Transistor #(.\type ("n")) transistor_35 (.in(left_top), .out(mid), .gate(_8));
  Transistor #(.\type ("n")) transistor_36 (.in(_4), .out(right_bot), .gate(_4));
  Transistor #(.\type ("n")) transistor_37 (.in(right_bot), .out(mid), .gate(_4));
  Transistor #(.\type ("n")) transistor_38 (.in(left_bot), .out(bot), .gate(_8));
  Transistor #(.\type ("n")) transistor_39 (.in(mid), .out(left_bot), .gate(_8));
  Transistor #(.\type ("n")) transistor_40 (.in(left_top), .out(right_top), .gate(_4));
  Transistor #(.\type ("n")) transistor_41 (.in(mid), .out(left_top), .gate(_4));
  Transistor #(.\type ("n")) transistor_42 (.in(bot), .out(right_bot), .gate(_8));
  Transistor #(.\type ("n")) transistor_43 (.in(_9), .out(right_top), .gate(_9));
  Transistor #(.\type ("n")) transistor_44 (.in(right_top), .out(top), .gate(_9));
  Transistor #(.\type ("n")) transistor_45 (.in(top), .out(left_top), .gate(_9));
  _7_Segment_Display u_7_segment_display_1 (
    .g(mid), .f(left_top), .a(top), .b(right_top), .e(left_bot), .d(bot), .c(right_bot));  // open: dp
  Transistor #(.\type ("n")) transistor_46 (.in(mid), .out(right_bot), .gate(_9));
  Transistor #(.\type ("n")) transistor_47 (.in(left_top), .out(mid), .gate(_9));
endmodule
